// Logisim project imm-gen.circ as structural Verilog: 1 circuit, main circuit imm_gen
module imm_gen (
  input  [31:0] inst,
  input  [2:0] ImmSel,
  output [31:0] imm
);


  assign imm = {32{1'b0}};

  // Other names for the same wires on the sheet: B7 = inst[7]; B8_11[3:0] = inst[11:8]; B12_14[2:0] = inst[14:12];
  //   B15_19[4:0] = inst[19:15]; B20_24[4:0] = inst[24:20]; B25_30[5:0] = inst[30:25]; B31 = inst[31]

  // Notes on the sheet:
  //   INPUTS to your circuit
  //   DON'T CHANGE THE LOCATIONS OF THE INPUTS AND OUTPUTS!
  //   OUTPUT from your circuit
endmodule
